// Logisim project Data Fetching.circ as structural Verilog
module main (
  input  in_1,
  input  in_2,
  input  in_3,
  output [31:0] out_4,
  output [31:0] out_5
);

  wire clock_1_out, immediate_datapath_1_branch_taken, undriven;
  wire [23:0] bit_extender_1_out;
  wire [31:0] adder_1_out, adder_2_out, IMM_FORB_TYPE, multiplexer_1_out, ram_1_data, register_1_q,
       shifter_1_out;

  Adder #(.width(32)) adder_1 (.a(32'h4), .b(register_1_q), .out(adder_1_out));  // open: cin, cout
  Multiplexer #(.width(32)) multiplexer_1 (
    .in0(adder_1_out), .in1(adder_2_out), .out(multiplexer_1_out), .sel(immediate_datapath_1_branch_taken));  // open: en
  Clock clock_1 (.out(clock_1_out));
  Adder #(.width(32)) adder_2 (.a(adder_1_out), .b(IMM_FORB_TYPE), .out(adder_2_out));  // open: cin, cout
  Register #(.width(32)) register_1 (
    .D(multiplexer_1_out), .en(undriven), .Q(register_1_q), .clk(clock_1_out), .clr(in_3));
  Shifter #(.width(32), .shift("lr")) shifter_1 (.in(register_1_q), .\dist (5'b00010), .out(shifter_1_out));
  Bit_Extender #(.in_width(32), .out_width(24)) bit_extender_1 (.in(shifter_1_out), .out(bit_extender_1_out));
  RAM #(.addrWidth(24), .dataWidth(32)) ram_1 (
    .addr(bit_extender_1_out), .data(ram_1_data), .clk(clock_1_out));  // open: sel, ld, clr
  immediate_datapath immediate_datapath_1 (
    .store(in_1), .load(in_2), .Inputinstruction(ram_1_data), .clk(clock_1_out), .ram_data(out_4),
    .reset(in_3), .rd(out_5), .branch_taken(immediate_datapath_1_branch_taken), .IMM_FOR_b_TYPE(IMM_FORB_TYPE));
endmodule

module R_Type_inst (
  input  [31:0] in_1,
  output [2:0] Funct3,
  output [6:0] Opcode,
  output [4:0] RD,
  output [4:0] RS1,
  output [4:0] RS2,
  output [6:0] Funct7
);


  assign Funct3 = in_1[14:12];
  assign Funct7 = in_1[31:25];
  assign Opcode = in_1[6:0];
  assign RD = in_1[11:7];
  assign RS1 = in_1[19:15];
  assign RS2 = in_1[24:20];

  // Notes on the sheet:
  //   R_Type
endmodule

// Immediate generator
module Immediate_Generator (
  input  [31:0] Inst_Input,
  output [31:0] Immediate
);

  wire comparator_1_eq, comparator_2_eq, comparator_3_eq, comparator_4_eq, comparator_5_eq, comparator_6_eq,
       comparator_7_eq;
  wire [2:0] priority_encoder_1_out;
  wire [3:0] b_type_immediate_1_imm_4_1;
  wire [4:0] s_type_immediate_1_imm_4_0;
  wire [5:0] b_type_immediate_1_out_8;
  wire [6:0] b_type_immediate_1_out_2, i_type_immediate_1_out_2, i_type_immediate_2_out_2,
       j_type_immediate_1_out_2, r_type_inst_1_opcode, s_type_immediate_1_out_2, s_type_immediate_1_out_7,
       u_type_immediate_1_out_2;
  wire [7:0] j_type_immediate_1_out_4;
  wire [9:0] j_type_immediate_1_out_6;
  wire [11:0] b_type_immediate_1_imm_11, i_type_immediate_1_out_6, i_type_immediate_2_out_6;
  wire [19:0] u_type_immediate_1_out_4;
  wire [19:8] j_type_immediate_1_imm_11;
  wire [31:0] B_Type, I_Type, I_Typefor_lw, J_Type, S_Type, U_Type;

  I_Type_Immediate i_type_immediate_1 (
    .in_1(Inst_Input), .out_2(i_type_immediate_1_out_2), .out_6(i_type_immediate_1_out_6));  // open: RD, Funct3, RS1
  S_Type_Immediate s_type_immediate_1 (
    .in_1(Inst_Input), .out_2(s_type_immediate_1_out_2), .IMM_4_0(s_type_immediate_1_imm_4_0),
    .out_7(s_type_immediate_1_out_7));  // open: Funct3, RS1, RS2
  B_Type_Immediate b_type_immediate_1 (
    .in_1(Inst_Input), .out_2(b_type_immediate_1_out_2), .IMM_11(b_type_immediate_1_imm_11[0]),
    .IMM_4_1(b_type_immediate_1_imm_4_1), .out_8(b_type_immediate_1_out_8),
    .IMM_12(b_type_immediate_1_imm_11[11]));  // open: Funct_3, RS1, RS2
  J_Type_Immediate j_type_immediate_1 (
    .in_1(Inst_Input), .out_2(j_type_immediate_1_out_2), .out_4(j_type_immediate_1_out_4),
    .IMM_11(j_type_immediate_1_imm_11[8]), .out_6(j_type_immediate_1_out_6),
    .IMM_20(j_type_immediate_1_imm_11[19]));  // open: RD
  U_Type_Immediate u_type_immediate_1 (
    .in_1(Inst_Input), .out_2(u_type_immediate_1_out_2), .out_4(u_type_immediate_1_out_4));  // open: RD
  R_Type_inst r_type_inst_1 (.in_1(Inst_Input), .Opcode(r_type_inst_1_opcode));  // open: Funct3, RD, RS1, RS2, Funct7
  assign I_Type = {{20{1'b0}}, i_type_immediate_1_out_6};  // Bit_Extender bit_extender_1
  assign U_Type = {{12{1'b0}}, u_type_immediate_1_out_4};  // Bit_Extender bit_extender_2
  Comparator #(.width(7)) comparator_1 (
    .a(r_type_inst_1_opcode), .b(7'b0110011), .eq(comparator_1_eq));  // open: gt, lt
  Comparator #(.width(7)) comparator_2 (
    .a(i_type_immediate_1_out_2), .b(7'b0010011), .eq(comparator_2_eq));  // open: gt, lt
  Comparator #(.width(7)) comparator_3 (
    .a(s_type_immediate_1_out_2), .b(7'b0100011), .eq(comparator_3_eq));  // open: gt, lt
  assign S_Type = {{20{1'b0}}, {s_type_immediate_1_out_7, s_type_immediate_1_imm_4_0}};  // Bit_Extender bit_extender_3
  Comparator #(.width(7)) comparator_4 (
    .a(b_type_immediate_1_out_2), .b(7'b1100011), .eq(comparator_4_eq));  // open: gt, lt
  assign B_Type = {{20{1'b0}}, {b_type_immediate_1_imm_11[11], b_type_immediate_1_out_8, b_type_immediate_1_imm_4_1, b_type_immediate_1_imm_11[0]}};  // Bit_Extender bit_extender_4
  Comparator #(.width(7)) comparator_5 (
    .a(j_type_immediate_1_out_2), .b(7'b1101111), .eq(comparator_5_eq));  // open: gt, lt
  assign J_Type = {{12{1'b0}}, {j_type_immediate_1_imm_11[19], j_type_immediate_1_out_6, j_type_immediate_1_imm_11[8], j_type_immediate_1_out_4}};  // Bit_Extender bit_extender_5
  Comparator #(.width(7)) comparator_6 (
    .a(u_type_immediate_1_out_2), .b(7'b0110111), .eq(comparator_6_eq));  // open: gt, lt
  I_Type_Immediate i_type_immediate_2 (
    .in_1(Inst_Input), .out_2(i_type_immediate_2_out_2), .out_6(i_type_immediate_2_out_6));  // open: RD, Funct3, RS1
  assign I_Typefor_lw = {{20{1'b0}}, i_type_immediate_2_out_6};  // Bit_Extender bit_extender_6
  Priority_Encoder priority_encoder_1 (
    .in0(comparator_2_eq), .in1(comparator_3_eq), .in2(comparator_4_eq), .in3(comparator_5_eq),
    .in4(comparator_6_eq), .in5(comparator_1_eq), .in6(comparator_7_eq), .out(priority_encoder_1_out));  // open: in7, en_in, gs, en_out
  Comparator #(.width(7)) comparator_7 (
    .a(i_type_immediate_2_out_2), .b(7'b0000011), .eq(comparator_7_eq));  // open: gt, lt
  Multiplexer #(.select(3), .width(32), .enable("false")) multiplexer_1 (
    .in0(I_Type), .in1(S_Type), .in2(B_Type), .in3(J_Type), .in4(U_Type), .in5({32{1'b0}}),
    .in6(I_Typefor_lw), .out(Immediate), .sel(priority_encoder_1_out));  // open: in7

  // Other names for the same wires on the sheet: Input[31:0] = Inst_Input
endmodule

module Register_File (
  input  [4:0] RSI,
  input  [4:0] RSI2,
  input  [4:0] RDInstruction,
  input  clk,
  input  [31:0] RDValue,
  input  Write_Enable,
  output [31:0] RS1out,
  output [31:0] RS2out
);

  wire x0, x1, x2, x3, x4, x5, x6, x7, x8, x9, x10, x11, x12, x13, x14, x15, x16, x17, x18, x19, x20, x21,
       x22, x23, x24, x25, x26, x27, x28, x29, x30, x31;
  wire [31:0] x0out, x1out, x2out, x3out, x4out, x5out, x6out, x7out, x8out, x9out, x10out, x11out, x12out,
       x14out, x16out, x17out, x18out, x19out, x20out, x21out, x22out, x23out, x24out, x25out, x26out,
       x27out, x28out, x29out, x30out, x31out;

  Demultiplexer #(.select(5)) demultiplexer_1 (
    .out0(x0), .out1(x1), .out2(x2), .out3(x3), .out4(x4), .out5(x5), .out6(x6), .out7(x7), .out8(x8),
    .out9(x9), .out10(x10), .out11(x11), .out12(x12), .out13(x13), .out14(x14), .out15(x15), .out16(x16),
    .out17(x17), .out18(x18), .out19(x19), .out20(x20), .out21(x21), .out22(x22), .out23(x23), .out24(x24),
    .out25(x25), .out26(x26), .out27(x27), .out28(x28), .out29(x29), .out30(x30), .out31(x31),
    .in(Write_Enable), .sel(RDInstruction));  // open: en
  Register #(.width(32)) u_X0 (.D(RDValue), .en(x0), .Q(x0out), .clk(clk));  // open: clr
  Register #(.width(32)) u_X4 (.D(RDValue), .en(x4), .Q(x4out), .clk(clk));  // open: clr
  Register #(.width(32)) u_X8 (.D(RDValue), .en(x8), .Q(x8out), .clk(clk));  // open: clr
  Register #(.width(32)) u_X12 (.D(RDValue), .en(x12), .Q(x12out), .clk(clk));  // open: clr
  Register #(.width(32)) u_X16 (.D(RDValue), .en(x16), .Q(x16out), .clk(clk));  // open: clr
  Register #(.width(32)) u_X20 (.D(RDValue), .en(x20), .Q(x20out), .clk(clk));  // open: clr
  Register #(.width(32)) u_X24 (.D(RDValue), .en(x24), .Q(x24out), .clk(clk));  // open: clr
  Register #(.width(32)) u_X28 (.D(RDValue), .en(x28), .Q(x28out), .clk(clk));  // open: clr
  Register #(.width(32)) u_X1 (.D(RDValue), .en(x1), .Q(x1out), .clk(clk));  // open: clr
  Register #(.width(32)) u_X5 (.D(RDValue), .en(x5), .Q(x5out), .clk(clk));  // open: clr
  Register #(.width(32)) u_X9 (.D(RDValue), .en(x9), .Q(x9out), .clk(clk));  // open: clr
  Register #(.width(32)) u_X13 (.D(RDValue), .en(x13), .Q(x12out), .clk(clk));  // open: clr
  Register #(.width(32)) u_X17 (.D(RDValue), .en(x17), .Q(x17out), .clk(clk));  // open: clr
  Register #(.width(32)) u_X21 (.D(RDValue), .en(x21), .Q(x21out), .clk(clk));  // open: clr
  Register #(.width(32)) u_X25 (.D(RDValue), .en(x25), .Q(x25out), .clk(clk));  // open: clr
  Register #(.width(32)) u_X29 (.D(RDValue), .en(x29), .Q(x29out), .clk(clk));  // open: clr
  Register #(.width(32)) u_X2 (.D(RDValue), .en(x2), .Q(x2out), .clk(clk));  // open: clr
  Register #(.width(32)) u_X6 (.D(RDValue), .en(x6), .Q(x6out), .clk(clk));  // open: clr
  Register #(.width(32)) u_X10 (.D(RDValue), .en(x10), .Q(x10out), .clk(clk));  // open: clr
  Register #(.width(32)) u_X14 (.D(RDValue), .en(x14), .Q(x14out), .clk(clk));  // open: clr
  Register #(.width(32)) u_X18 (.D(RDValue), .en(x18), .Q(x18out), .clk(clk));  // open: clr
  Register #(.width(32)) u_X22 (.D(RDValue), .en(x22), .Q(x22out), .clk(clk));  // open: clr
  Register #(.width(32)) u_X26 (.D(RDValue), .en(x26), .Q(x26out), .clk(clk));  // open: clr
  Register #(.width(32)) u_X30 (.D(RDValue), .en(x30), .Q(x30out), .clk(clk));  // open: clr
  Register #(.width(32)) u_X3 (.D(RDValue), .en(x3), .Q(x3out), .clk(clk));  // open: clr
  Register #(.width(32)) u_X7 (.D(RDValue), .en(x7), .Q(x7out), .clk(clk));  // open: clr
  Register #(.width(32)) u_X11 (.D(RDValue), .en(x11), .Q(x11out), .clk(clk));  // open: clr
  Register #(.width(32)) u_X15 (.D(RDValue), .en(x15), .Q(x14out), .clk(clk));  // open: clr
  Register #(.width(32)) u_X19 (.D(RDValue), .en(x19), .Q(x19out), .clk(clk));  // open: clr
  Register #(.width(32)) u_X23 (.D(RDValue), .en(x23), .Q(x23out), .clk(clk));  // open: clr
  Register #(.width(32)) u_X27 (.D(RDValue), .en(x27), .Q(x27out), .clk(clk));  // open: clr
  Register #(.width(32)) u_X31 (.D(RDValue), .en(x31), .Q(x31out), .clk(clk));  // open: clr
  Multiplexer #(.select(5), .width(32)) multiplexer_1 (
    .in0(x0out), .in1(x1out), .in2(x2out), .in3(x3out), .in4(x4out), .in5(x5out), .in6(x6out), .in7(x7out),
    .in8(x8out), .in9(x9out), .in10(x10out), .in11(x11out), .in12(x12out), .in13(x12out), .in14(x14out),
    .in15(x14out), .in16(x16out), .in17(x17out), .in18(x18out), .in19(x19out), .in20(x20out), .in21(x21out),
    .in22(x22out), .in23(x23out), .in24(x24out), .in25(x25out), .in26(x26out), .in27(x27out), .in28(x28out),
    .in29(x29out), .in30(x30out), .in31(x31out), .out(RS1out), .sel(RSI));  // open: en
  Multiplexer #(.select(5), .width(32)) multiplexer_2 (
    .in0(x0out), .in1(x1out), .in2(x2out), .in3(x3out), .in4(x4out), .in5(x5out), .in6(x6out), .in7(x7out),
    .in8(x8out), .in9(x9out), .in10(x10out), .in11(x11out), .in12(x12out), .in13(x12out), .in14(x14out),
    .in15(x14out), .in16(x16out), .in17(x17out), .in18(x18out), .in19(x19out), .in20(x20out), .in21(x21out),
    .in22(x22out), .in23(x23out), .in24(x24out), .in25(x25out), .in26(x26out), .in27(x27out), .in28(x28out),
    .in29(x29out), .in30(x30out), .in31(x31out), .out(RS2out), .sel(RSI2));  // open: en

  // Other names for the same wires on the sheet: RDI[4:0] = RDInstruction; RSI1[4:0] = RSI; W_E = Write_Enable;
  //   x13out[31:0] = x12out; x15out[31:0] = x14out
endmodule

module PC (
  input  in_1,
  input  [31:0] in_2,
  input  in_3,
  input  [4:0] in_4,
  output [31:0] out_5,
  output out_6
);

  wire clock_1_out, undriven;
  wire [23:0] bit_extender_1_out;
  wire [31:0] register_1_q, shifter_1_out;

  Adder #(.width(32)) adder_1 (.a(in_2), .b(register_1_q), .out(out_5), .cin(in_1), .cout(out_6));
  Clock clock_1 (.out(clock_1_out));
  Register #(.width(32)) register_1 (.D(out_5), .en(undriven), .Q(register_1_q), .clk(clock_1_out), .clr(in_3));
  Shifter #(.width(32), .shift("lr")) shifter_1 (.in(register_1_q), .\dist (in_4), .out(shifter_1_out));
  Bit_Extender #(.in_width(32), .out_width(24)) bit_extender_1 (.in(shifter_1_out), .out(bit_extender_1_out));
  RAM #(.addrWidth(24), .dataWidth(32)) ram_1 (
    .addr(bit_extender_1_out), .clk(clock_1_out));  // open: data, sel, ld, clr
endmodule

module I_Type_Immediate (
  input  [31:0] in_1,
  output [6:0] out_2,
  output [4:0] RD,
  output [2:0] Funct3,
  output [4:0] RS1,
  output [11:0] out_6
);


  assign Funct3 = in_1[14:12];
  assign out_2 = in_1[6:0];
  assign out_6 = in_1[31:20];
  assign RD = in_1[11:7];
  assign RS1 = in_1[19:15];

  // Notes on the sheet:
  //   Opcode
  //   IMM
endmodule

module S_Type_Immediate (
  input  [31:0] in_1,
  output [6:0] out_2,
  output [4:0] IMM_4_0,
  output [2:0] Funct3,
  output [4:0] RS1,
  output [4:0] RS2,
  output [6:0] out_7
);


  assign Funct3 = in_1[14:12];
  assign IMM_4_0 = in_1[11:7];
  assign out_2 = in_1[6:0];
  assign out_7 = in_1[31:25];
  assign RS1 = in_1[19:15];
  assign RS2 = in_1[24:20];

  // Notes on the sheet:
  //   OPCODE
  //   IMM[31:25]
endmodule

module B_Type_Immediate (
  input  [31:0] in_1,
  output [6:0] out_2,
  output IMM_11,
  output [3:0] IMM_4_1,
  output [2:0] Funct_3,
  output [4:0] RS1,
  output [4:0] RS2,
  output [5:0] out_8,
  output IMM_12
);


  assign Funct_3 = in_1[14:12];
  assign IMM_4_1 = in_1[11:8];
  assign IMM_11 = in_1[7];
  assign IMM_12 = in_1[31];
  assign out_2 = in_1[6:0];
  assign out_8 = in_1[30:25];
  assign RS1 = in_1[19:15];
  assign RS2 = in_1[24:20];

  // Notes on the sheet:
  //   Opcode
  //   IMM 10:5
endmodule

module J_Type_Immediate (
  input  [31:0] in_1,
  output [6:0] out_2,
  output [4:0] RD,
  output [7:0] out_4,
  output IMM_11,
  output [9:0] out_6,
  output IMM_20
);


  assign IMM_11 = in_1[20];
  assign IMM_20 = in_1[31];
  assign out_2 = in_1[6:0];
  assign out_4 = in_1[19:12];
  assign out_6 = in_1[30:21];
  assign RD = in_1[11:7];

  // Notes on the sheet:
  //   OPCODE
  //   IMM[19:12]
  //   IMM[10:1]
endmodule

module U_Type_Immediate (
  input  [31:0] in_1,
  output [6:0] out_2,
  output [4:0] RD,
  output [19:0] out_4
);


  assign out_2 = in_1[6:0];
  assign out_4 = in_1[31:12];
  assign RD = in_1[11:7];

  // Notes on the sheet:
  //   Opcode
  //   IMM[31:12]
endmodule

module DataPath (
  input  [31:0] in_1,
  output [31:0] out_2,
  output [31:0] out_3
);

  wire clock_1_out, control_unit_1_rs2_imm_sel;
  wire [3:0] control_unit_1_selbit_2;
  wire [4:0] r_type_inst_1_rd, r_type_inst_1_rs1, r_type_inst_1_rs2;
  wire [31:0] register_file_1_rs2out;

  Clock clock_1 (.out(clock_1_out));
  R_Type_inst r_type_inst_1 (
    .in_1(in_1), .RD(r_type_inst_1_rd), .RS1(r_type_inst_1_rs1), .RS2(r_type_inst_1_rs2));  // open: Funct3, Opcode, Funct7
  Register_File register_file_1 (
    .RSI(r_type_inst_1_rs1), .RSI2(r_type_inst_1_rs2), .RDInstruction(r_type_inst_1_rd), .clk(clock_1_out),
    .RDValue(out_3), .Write_Enable(control_unit_1_rs2_imm_sel), .RS1out(out_2),
    .RS2out(register_file_1_rs2out));
  Control_Unit control_unit_1 (
    .Instruction(in_1), .SelBit_2(control_unit_1_selbit_2), .rs2_imm_sel(control_unit_1_rs2_imm_sel));  // open: SelBit, wenb, output_for_sotre, Branch_enable
  ALU alu_1 (
    .dataA(out_2), .dataB(register_file_1_rs2out), .selector(control_unit_1_selbit_2), .dataD(out_3));  // open: selbit_for_unsigned, output_branch_taken

  // Notes on the sheet:
  //   00418133
endmodule

module ALU (
  input  [31:0] dataA,
  input  [31:0] dataB,
  input  [3:0] selector,
  input  selbit_for_unsigned,
  output [31:0] dataD,
  output output_branch_taken
);

  wire branch_1_bge_u, branch_1_breq, comparator_1_lt, comparator_2_lt;
  wire [31:0] adderout, andout, orout, sll, slt, sltunsigned, sra, srl, subtout, xorout;

  Adder #(.width(32)) adder_1 (.a(dataA), .b(dataB), .out(adderout));  // open: cin, cout
  Subtractor #(.width(32)) subtractor_1 (.a(dataA), .b(dataB), .out(subtout));  // open: bin, bout
  Shifter #(.width(32)) shifter_1 (.in(dataA), .\dist (dataB[4:0]), .out(sll));
  Comparator #(.width(32)) comparator_1 (.a(dataA), .b(dataB), .lt(comparator_1_lt));  // open: gt, eq
  Comparator #(.width(32), .mode("unsigned")) comparator_2 (
    .a(dataA), .b(dataB), .lt(comparator_2_lt));  // open: gt, eq
  assign xorout = dataA ^ dataB;  // XOR_Gate xor_1, 32 bits wide
  assign andout = dataA & dataB;  // AND_Gate and_1, 32 bits wide
  assign orout = dataA | dataB;  // OR_Gate or_1, 32 bits wide
  Shifter #(.width(32), .shift("lr")) shifter_2 (.in(dataA), .\dist (dataB[4:0]), .out(srl));
  Shifter #(.width(32), .shift("ar")) shifter_3 (.in(dataA), .\dist (dataB[4:0]), .out(sra));
  assign slt = {{31{1'b0}}, comparator_1_lt};  // Bit_Extender bit_extender_1
  assign sltunsigned = {{31{1'b0}}, comparator_2_lt};  // Bit_Extender bit_extender_2
  Branch branch_1 (
    .dataA(dataA), .dataB(dataB), .\unsigned (selbit_for_unsigned), .Breq(branch_1_breq),
    .bge_u(branch_1_bge_u));  // open: blt_u
  Multiplexer #(.select(4), .width(32)) multiplexer_1 (
    .in0(adderout), .in1(sll), .in2(slt), .in3(sltunsigned), .in4(xorout), .in5(srl), .in6(orout),
    .in7(andout), .in8(subtout), .in13(sra), .out(dataD), .sel(selector));  // open: in9, in10, in11, in12, in14, in15, en
  Comparator #(.width(1)) comparator_3 (.a(branch_1_breq), .b(1'b1), .eq(output_branch_taken));  // open: gt, lt

  // Other names for the same wires on the sheet: dataAi[31:0] = dataA; dataBi[31:0] = dataB;
  //   dataBshift[4:0] = dataB[4:0]
endmodule

module Branch (
  input  [31:0] dataA,
  input  [31:0] dataB,
  input  \unsigned ,
  output blt_u,
  output Breq,
  output bge_u
);

  wire comparator_1_gt, comparator_1_lt, comparator_2_eq, comparator_2_gt, comparator_2_lt, or_1_out,
       or_2_out;

  Comparator #(.width(32)) comparator_1 (.a(dataA), .b(dataB), .gt(comparator_1_gt), .eq(Breq), .lt(comparator_1_lt));
  Comparator #(.width(32), .mode("unsigned")) comparator_2 (
    .a(dataA), .b(dataB), .gt(comparator_2_gt), .eq(comparator_2_eq), .lt(comparator_2_lt));
  Multiplexer multiplexer_1 (.in0(comparator_1_lt), .in1(comparator_2_lt), .out(blt_u), .sel(\unsigned ));  // open: en
  or or_1 (or_1_out, comparator_2_gt, comparator_2_eq);
  or or_2 (or_2_out, comparator_1_gt, Breq);
  Multiplexer multiplexer_2 (.in0(or_2_out), .in1(or_1_out), .out(bge_u), .sel(\unsigned ));  // open: en

  // Notes on the sheet:
  //   blt
  //   bltu
endmodule

// CU
module Control_Unit (
  input  [31:0] Instruction,
  input  [3:0] SelBit,
  output [3:0] SelBit_2,
  output wenb,
  output rs2_imm_sel,
  output output_for_sotre,
  output Branch_enable
);

  wire Add, Addi, Addr, And, Andi, Andr, Bge, Bgeu, Blt, Bltu, Bne, Breq, lb, lbu, lh, lhu, lw, OR, ORi, ORr,
       sb, sh, Sll, Slli, Sllr, Slt, Slti, Sltr, Sltu, Sltui, Sltur, Sra, Srai, Srar, Srl, Srli, Srlr, Sub,
       sw, Xor, Xori, Xorr;

  and and_1 (sw, ~Instruction[2], ~Instruction[3], ~Instruction[4], Instruction[5], ~Instruction[6], ~Instruction[12], Instruction[13], ~Instruction[14], ~Instruction[30]);  // AND_Gate
  and and_2 (sh, ~Instruction[2], ~Instruction[3], ~Instruction[4], Instruction[5], ~Instruction[6], Instruction[12], ~Instruction[13], ~Instruction[14], ~Instruction[30]);  // AND_Gate
  and and_3 (sb, ~Instruction[2], ~Instruction[3], ~Instruction[4], Instruction[5], ~Instruction[6], ~Instruction[12], ~Instruction[13], ~Instruction[14], ~Instruction[30]);  // AND_Gate
  and and_4 (lb, ~Instruction[2], ~Instruction[3], ~Instruction[4], ~Instruction[5], ~Instruction[6], ~Instruction[12], ~Instruction[13], ~Instruction[14], ~Instruction[30]);  // AND_Gate
  and and_5 (lh, ~Instruction[2], ~Instruction[3], ~Instruction[4], ~Instruction[5], ~Instruction[6], Instruction[12], ~Instruction[13], ~Instruction[14], ~Instruction[30]);  // AND_Gate
  and and_6 (lw, ~Instruction[2], ~Instruction[3], ~Instruction[4], ~Instruction[5], ~Instruction[6], ~Instruction[12], Instruction[13], ~Instruction[14], ~Instruction[30]);  // AND_Gate
  and and_7 (lbu, ~Instruction[2], ~Instruction[3], ~Instruction[4], ~Instruction[5], ~Instruction[6], ~Instruction[12], ~Instruction[13], Instruction[14], ~Instruction[30]);  // AND_Gate
  and and_8 (lhu, ~Instruction[2], ~Instruction[3], ~Instruction[4], ~Instruction[5], ~Instruction[6], Instruction[12], ~Instruction[13], Instruction[14], ~Instruction[30]);  // AND_Gate
  and and_9 (Addr, ~Instruction[2], ~Instruction[3], Instruction[4], Instruction[5], ~Instruction[6], ~Instruction[12], ~Instruction[13], ~Instruction[14], ~Instruction[30]);  // AND_Gate
  and and_10 (Sub, ~Instruction[2], ~Instruction[3], Instruction[4], Instruction[5], ~Instruction[6], ~Instruction[12], ~Instruction[13], ~Instruction[14], Instruction[30]);  // AND_Gate
  and and_11 (Sllr, ~Instruction[2], ~Instruction[3], Instruction[4], Instruction[5], ~Instruction[6], Instruction[12], ~Instruction[13], ~Instruction[14], ~Instruction[30]);  // AND_Gate
  and and_12 (Sltr, ~Instruction[2], ~Instruction[3], Instruction[4], Instruction[5], ~Instruction[6], ~Instruction[12], Instruction[13], ~Instruction[14], ~Instruction[30]);  // AND_Gate
  and and_13 (Sltur, ~Instruction[2], ~Instruction[3], Instruction[4], Instruction[5], ~Instruction[6], Instruction[12], Instruction[13], ~Instruction[14], ~Instruction[30]);  // AND_Gate
  and and_14 (Xorr, ~Instruction[2], ~Instruction[3], Instruction[4], Instruction[5], ~Instruction[6], ~Instruction[12], ~Instruction[13], Instruction[14], ~Instruction[30]);  // AND_Gate
  and and_15 (Srlr, ~Instruction[2], ~Instruction[3], Instruction[4], Instruction[5], ~Instruction[6], Instruction[12], ~Instruction[13], Instruction[14], ~Instruction[30]);  // AND_Gate
  and and_16 (Srar, ~Instruction[2], ~Instruction[3], Instruction[4], Instruction[5], ~Instruction[6], Instruction[12], ~Instruction[13], Instruction[14], Instruction[30]);  // AND_Gate
  and and_17 (ORr, ~Instruction[2], ~Instruction[3], Instruction[4], Instruction[5], ~Instruction[6], ~Instruction[12], Instruction[13], Instruction[14], ~Instruction[30]);  // AND_Gate
  and and_18 (Andr, ~Instruction[2], ~Instruction[3], Instruction[4], Instruction[5], ~Instruction[6], Instruction[12], Instruction[13], Instruction[14], ~Instruction[30]);  // AND_Gate
  and and_19 (Srai, ~Instruction[2], ~Instruction[3], Instruction[4], ~Instruction[5], ~Instruction[6], Instruction[12], ~Instruction[13], Instruction[14], Instruction[30]);  // AND_Gate
  or or_1 (Sra, Srar, Srai);
  and and_20 (ORi, ~Instruction[2], ~Instruction[3], Instruction[4], ~Instruction[5], ~Instruction[6], ~Instruction[12], Instruction[13], Instruction[14], ~Instruction[30]);  // AND_Gate
  or or_2 (OR, ORr, ORi);
  and and_21 (Andi, ~Instruction[2], ~Instruction[3], Instruction[4], ~Instruction[5], ~Instruction[6], Instruction[12], Instruction[13], Instruction[14], ~Instruction[30]);  // AND_Gate
  or or_3 (And, Andr, Andi);
  and and_22 (Addi, ~Instruction[2], ~Instruction[3], Instruction[4], ~Instruction[5], ~Instruction[6], ~Instruction[12], ~Instruction[13], ~Instruction[14], ~Instruction[30]);  // AND_Gate
  or or_4 (Add, Addr, Addi);
  or or_5 (SelBit_2[3], Sub, Sra);
  or or_6 (SelBit_2[2], Xor, Srl, Sra, OR, And);
  or or_7 (SelBit_2[1], Slt, Sltu, OR, And);
  or or_8 (SelBit_2[0], Sll, Sltu, Srl, Sra, And);
  and and_23 (Slli, ~Instruction[2], ~Instruction[3], Instruction[4], ~Instruction[5], ~Instruction[6], Instruction[12], ~Instruction[13], ~Instruction[14], ~Instruction[30]);  // AND_Gate
  or or_9 (Sll, Sllr, Slli);
  and and_24 (Slti, ~Instruction[2], ~Instruction[3], Instruction[4], ~Instruction[5], ~Instruction[6], ~Instruction[12], Instruction[13], ~Instruction[14], ~Instruction[30]);  // AND_Gate
  or or_10 (Slt, Sltr, Slti);
  and and_25 (Sltui, ~Instruction[2], ~Instruction[3], Instruction[4], ~Instruction[5], ~Instruction[6], Instruction[12], Instruction[13], ~Instruction[14], ~Instruction[30]);  // AND_Gate
  or or_11 (Sltu, Sltur, Sltui);
  and and_26 (Xori, ~Instruction[2], ~Instruction[3], Instruction[4], ~Instruction[5], ~Instruction[6], ~Instruction[12], ~Instruction[13], Instruction[14], ~Instruction[30]);  // AND_Gate
  or or_12 (Xor, Xorr, Xori);
  and and_27 (Srli, ~Instruction[2], ~Instruction[3], Instruction[4], ~Instruction[5], ~Instruction[6], Instruction[12], ~Instruction[13], Instruction[14], ~Instruction[30]);  // AND_Gate
  or or_13 (Srl, Srlr, Srli);
  or or_14 (Branch_enable, Breq, Bne, Blt, Bge, Bltu, Bgeu);
  Multiplexer #(.select(4)) multiplexer_1 (
    .in0(sw), .in2(sh), .in4(sb), .out(output_for_sotre), .sel(SelBit));  // open: in1, in3, in5, in6, in7, in8, in9, in10, in11, in12, in13, in14, in15, en
  and and_28 (Breq, ~Instruction[2], ~Instruction[3], ~Instruction[4], Instruction[5], Instruction[6], ~Instruction[12], ~Instruction[13], ~Instruction[14], ~Instruction[30]);  // AND_Gate
  and and_29 (Bne, ~Instruction[2], ~Instruction[3], ~Instruction[4], Instruction[5], Instruction[6], Instruction[12], ~Instruction[13], ~Instruction[14], ~Instruction[30]);  // AND_Gate
  and and_30 (Blt, ~Instruction[2], ~Instruction[3], ~Instruction[4], Instruction[5], Instruction[6], ~Instruction[12], ~Instruction[13], Instruction[14], ~Instruction[30]);  // AND_Gate
  and and_31 (Bge, ~Instruction[2], ~Instruction[3], ~Instruction[4], Instruction[5], Instruction[6], Instruction[12], ~Instruction[13], Instruction[14], ~Instruction[30]);  // AND_Gate
  and and_32 (Bltu, ~Instruction[2], ~Instruction[3], ~Instruction[4], Instruction[5], Instruction[6], ~Instruction[12], Instruction[13], Instruction[14], ~Instruction[30]);  // AND_Gate
  and and_33 (Bgeu, ~Instruction[2], ~Instruction[3], ~Instruction[4], Instruction[5], Instruction[6], Instruction[12], Instruction[13], Instruction[14], ~Instruction[30]);  // AND_Gate
  or or_15 (wenb, lb, lh, Addr, Sub, Sllr, Sltr, Sltur, Xorr, Srlr, Srar, ORr, Andr, Srai, lw, ORi, Andi, Srli, Xori, Sltui, Slti, Slli, Addi, sw, sh, sb, lbu, lhu);
  or or_16 (rs2_imm_sel, lb, lh, Addi, sw, sh, sb, Slli, Srai, lw, ORi, Andi, Srli, Xori, Sltui, Slti, lbu, lhu);

  // Other names for the same wires on the sheet: i0 = Instruction[2]; i1 = Instruction[3]; i2 = Instruction[4];
  //   i3 = Instruction[5]; i4 = Instruction[6]; i5 = Instruction[12]; i6 = Instruction[13]; i7 = Instruction[14];
  //   i8 = Instruction[30]; out0 = SelBit_2[0]; out1 = SelBit_2[1]; out2 = SelBit_2[2]; out3 = SelBit_2[3]

  // Notes on the sheet:
  //   Zainkhan5
endmodule

module immediate_datapath (
  input  store,
  input  reset,
  input  load,
  input  [31:0] Inputinstruction,
  input  clk,
  output [31:0] ram_data,
  output [31:0] rd,
  output branch_taken,
  output [31:0] IMM_FOR_b_TYPE
);

  wire alu_1_output_branch_taken, control_unit_1_branch_enable, control_unit_1_rs2_imm_sel,
       control_unit_1_wenb;
  wire [3:0] control_unit_1_selbit_2;
  wire [23:0] bit_extender_1_out;
  wire [31:0] alu_control_for_imm_1_output_for_datab, bit_extender_2_out, bit_extender_3_out,
       output_data_for_store, register_file_1_rs1out, rs2_data_to_save, shifter_1_out;

  Register_File register_file_1 (
    .RSI(Inputinstruction[19:15]), .RSI2(Inputinstruction[24:20]), .RDInstruction(Inputinstruction[11:7]),
    .clk(clk), .RDValue(rd), .Write_Enable(control_unit_1_wenb), .RS1out(register_file_1_rs1out),
    .RS2out(rs2_data_to_save));
  Immediate_Generator immediate_generator_1 (.Inst_Input(Inputinstruction), .Immediate(IMM_FOR_b_TYPE));
  Control_Unit control_unit_1 (
    .Instruction(Inputinstruction), .SelBit_2(control_unit_1_selbit_2), .wenb(control_unit_1_wenb),
    .rs2_imm_sel(control_unit_1_rs2_imm_sel), .Branch_enable(control_unit_1_branch_enable));  // open: SelBit, output_for_sotre
  ALU_Control_for_Imm alu_control_for_imm_1 (
    .RS2(rs2_data_to_save), .IMMG_input(IMM_FOR_b_TYPE), .sel_bit_for_rs2_imm(control_unit_1_rs2_imm_sel),
    .output_for_dataB(alu_control_for_imm_1_output_for_datab));
  Shifter #(.width(32), .shift("lr")) shifter_1 (.in(rd), .\dist (5'b00010), .out(shifter_1_out));
  Bit_Extender #(.in_width(32), .out_width(24)) bit_extender_1 (.in(shifter_1_out), .out(bit_extender_1_out));
  ALU alu_1 (
    .dataA(register_file_1_rs1out), .dataB(alu_control_for_imm_1_output_for_datab),
    .selector(control_unit_1_selbit_2), .selbit_for_unsigned(control_unit_1_branch_enable), .dataD(rd),
    .output_branch_taken(alu_1_output_branch_taken));
  and and_1 (branch_taken, alu_1_output_branch_taken, control_unit_1_branch_enable);
  assign bit_extender_2_out = {{24{1'b0}}, rs2_data_to_save[7:0]};  // Bit_Extender bit_extender_2
  assign bit_extender_3_out = {{16{1'b0}}, rs2_data_to_save[15:0]};  // Bit_Extender bit_extender_3
  RAM #(.addrWidth(24), .dataWidth(32), .bus("separate")) ram_1 (
    .addr(bit_extender_1_out), .din(output_data_for_store), .data(ram_data), .str(store), .sel(1'b1),
    .clk(clk), .ld(load), .clr(reset));
  Multiplexer #(.select(4), .width(32)) multiplexer_1 (
    .in0(rs2_data_to_save), .in2(bit_extender_3_out), .in4(bit_extender_2_out), .out(output_data_for_store),
    .sel(control_unit_1_selbit_2));  // open: in1, in3, in5, in6, in7, in8, in9, in10, in11, in12, in13, in14, in15, en

  // Other names for the same wires on the sheet: RDI[4:0] = Inputinstruction[11:7];
  //   RS1[4:0] = Inputinstruction[19:15]; RS2[4:0] = Inputinstruction[24:20]
endmodule

// Alu control for immedtiate
module ALU_Control_for_Imm (
  input  [31:0] RS2,
  input  [31:0] IMMG_input,
  input  sel_bit_for_rs2_imm,
  output [31:0] output_for_dataB
);

  Multiplexer #(.width(32)) multiplexer_1 (
    .in0(RS2), .in1(IMMG_input), .out(output_for_dataB), .sel(sel_bit_for_rs2_imm));  // open: en
endmodule

module RS1_Immediate (
  input  [31:0] Rs1,
  input  [31:0] Imm,
  output [31:0] RS1_immediate
);

  Adder #(.width(32)) adder_1 (.a(Rs1), .b(Imm), .out(RS1_immediate));  // open: cin, cout
endmodule
